// Logisim project SAP1.circ as structural Verilog: 4 circuits, main circuit main
module main (
  input  [7:0] in_1
);

  wire A_clr, A_in, A_out, and_1_out, and_3_out, B_clr, B_in, B_out, CF, clk, clock_1_out, EO, FLAG_clr,
       FLAG_in, hlt, IR_clr, IR_in, IR_out, MAR_clr, MAR_in, MAR_out, not_1_out, not_2_out, OCU_2s, OCU_clr,
       OCU_in, output_controller_1_is_negative, PC_clr, PC_en, PC_in, PC_out, RAM_in, RAM_out, rst, SU, ZF;
  wire [3:0] buffer_1_out, instruction, IR_q, MAR_q, output_controller_1_out_1s, output_controller_1_out_10s,
       output_controller_1_out_100s, PC_data_p1;
  wire [7:0] A_reg_q, ALU_data_p1, B_reg_q;
  wire [7:4] buffer_1_out_2;

  assign {buffer_1_out_2, buffer_1_out} = in_1;  // Buffer buffer_1, 8 bits wide
  Pull_Resistor pull_resistor_1 (.node({buffer_1_out_2, buffer_1_out}));
  Clock clock_1 (.out(clock_1_out));
  not not_1 (not_1_out, rst);
  RAM #(.addrWidth(4), .asyncread("true"), .databus("bidir"), .\type ("nonvolatile")) ram_1 (
    .addr(MAR_q), .we(RAM_in), .oe(RAM_out), .clk(clk), .data({buffer_1_out_2, buffer_1_out}));
  and and_1 (and_1_out, clock_1_out, not_1_out);
  and and_2 (clk, and_1_out, not_2_out);
  not not_2 (not_2_out, hlt);
  // LedBar #(.inputtype("row"), .matrixcols(4)) PC_data: pin names not known; wires that end beside it: PC_data_p1
  Counter #(.max('hf), .width(4)) counter_1 (
    .load(PC_in), .D(buffer_1_out), .count(PC_en), .Q(PC_data_p1), .up(1'b1), .clk(clk), .clr(PC_clr));  // open: carry
  Register #(.width(4)) MAR (.D(buffer_1_out), .en(MAR_in), .clk(clk), .Q(MAR_q), .clr(MAR_clr));
  Register IR (.D({buffer_1_out_2, buffer_1_out}), .en(IR_in), .clk(clk), .Q({instruction, IR_q}), .clr(IR_clr));
  // LedBar #(.inputtype("row")) Bus_Value: pin names not known; wires that end beside it: {buffer_1_out_2, buffer_1_out}
  assign buffer_1_out = PC_out ? PC_data_p1 : 4'bz;  // Controlled_Buffer controlled_buffer_1
  assign buffer_1_out = MAR_out ? MAR_q : 4'bz;  // Controlled_Buffer controlled_buffer_2
  assign buffer_1_out = IR_out ? IR_q : 4'bz;  // Controlled_Buffer controlled_buffer_3
  // LedBar #(.inputtype("row"), .matrixcols(4)) Instruction_Parameter: pin names not known; wires that end beside it: IR_q
  // LedBar #(.inputtype("row"), .matrixcols(4)) Instruction: pin names not known; wires that end beside it: instruction
  _7_Segment_Display #(.decimalPoint("false")) u_7_segment_display_1 (.g(output_controller_1_is_negative));  // open: f, a, b, e, d, c
  // LedBar #(.inputtype("row")) ALU_data: pin names not known; wires that end beside it: ALU_data_p1
  Pull_Resistor pull_resistor_2 (.node({buffer_1_out_2, buffer_1_out}));
  Button Reset (.out(rst));
  and and_3 (and_3_out, clk, OCU_clr);
  or or_1 (and_3_out, OCU_clr, rst);
  Hex_Digit_Display #(.decimalPoint("false")) hex_digit_display_1 (.value(output_controller_1_out_100s));
  ALU alu_1 (
    .ALU_out({buffer_1_out_2, buffer_1_out}), .ALU_data(ALU_data_p1), .CF(CF), .ZF(ZF), .SU(SU),
    .B_in(B_reg_q), .A_in(A_reg_q), .FLAG_in(FLAG_in), .clk(clk), .FLAG_clr(FLAG_clr), .EO(EO));
  Pull_Resistor pull_resistor_3 (.node(and_3_out));
  Hex_Digit_Display #(.decimalPoint("false")) hex_digit_display_2 (.value(output_controller_1_out_10s));
  Hex_Digit_Display #(.decimalPoint("false")) hex_digit_display_3 (.value(output_controller_1_out_1s));
  Register A_reg (.D({buffer_1_out_2, buffer_1_out}), .en(A_in), .clk(clk), .Q(A_reg_q), .clr(A_clr));
  Register B_reg (.D({buffer_1_out_2, buffer_1_out}), .en(B_in), .clk(clk), .Q(B_reg_q), .clr(B_clr));
  Output_Controller output_controller_1 (
    .out_1s(output_controller_1_out_1s), .out_10s(output_controller_1_out_10s),
    .out_100s(output_controller_1_out_100s), .is_negative(output_controller_1_is_negative),
    .data_in({buffer_1_out_2, buffer_1_out}), .display_2s_comp(OCU_2s), .WE(OCU_in), .clk(clk),
    .rst(and_3_out));
  assign {buffer_1_out_2, buffer_1_out} = A_out ? A_reg_q : 8'bz;  // Controlled_Buffer controlled_buffer_4
  assign {buffer_1_out_2, buffer_1_out} = B_out ? B_reg_q : 8'bz;  // Controlled_Buffer controlled_buffer_5
  // LedBar #(.inputtype("row")) A_data: pin names not known; wires that end beside it: A_reg_q
  // LedBar #(.inputtype("row")) B_data: pin names not known; wires that end beside it: B_reg_q
  Control_Unit control_unit_1 (
    .A_out(A_out), .A_in(A_in), .A_clr(A_clr), .IR_out(IR_out), .IR_in(IR_in), .IR_clr(IR_clr), .EO(EO),
    .SU(SU), .OCU_2s(OCU_2s), .OCU_in(OCU_in), .OCU_clr(OCU_clr), .B_out(B_out), .B_in(B_in), .B_clr(B_clr),
    .MAR_out(MAR_out), .MAR_in(MAR_in), .MAR_clr(MAR_clr), .PC_en(PC_en), .PC_out(PC_out), .PC_in(PC_in),
    .PC_clr(PC_clr), .RAM_in(RAM_in), .RAM_out(RAM_out), .hlt(hlt), .FLAG_in(FLAG_in), .FLAG_clr(FLAG_clr),
    .clk(clk), .CF(CF), .ZF(ZF), .instruction(instruction), .rst(rst));

  // Notes on the sheet:
  //   buffer_1 drives only 1 and floats otherwise
  //   Clock
  //   and_3 drives only 1 and floats otherwise
  //   or_1 drives only 1 and floats otherwise
endmodule

module ALU (
  input  SU,
  input  [7:0] B_in,
  input  [7:0] A_in,
  input  EO,
  input  FLAG_in,
  input  clk,
  input  FLAG_clr,
  output [7:0] ALU_data,
  output [7:0] ALU_out,
  output CF,
  output ZF
);

  wire [1:0] adder_1_cout;
  wire [7:0] bit_extender_1_out, xor_1_out;

  assign bit_extender_1_out = {{7{SU}}, SU};  // Bit_Extender bit_extender_1
  assign xor_1_out = bit_extender_1_out ^ B_in;  // XOR_Gate xor_1, 8 bits wide
  Adder adder_1 (.a(xor_1_out), .b(A_in), .out(ALU_data), .cin(SU), .cout(adder_1_cout[0]));
  nor nor_1 (adder_1_cout[1], ALU_data[0], ALU_data[1], ALU_data[2], ALU_data[3], ALU_data[4], ALU_data[5], ALU_data[6], ALU_data[7]);
  assign ALU_out = EO ? ALU_data : 8'bz;  // Controlled_Buffer controlled_buffer_1
  Register #(.width(2)) Flags (.D(adder_1_cout), .en(FLAG_in), .clk(clk), .Q({ZF, CF}), .clr(FLAG_clr));

  // Notes on the sheet:
  //   SU: pull=down
  //   EO: pull=down
  //   CF: pull=down
  //   ZF: pull=down
  //   Hook up for led bar display to
  //   show internal alu state
  //   Actual controlled alu bus output
  //   ALU Flags
endmodule

module Output_Controller (
  input  [7:0] data_in,
  input  display_2s_comp,
  input  WE,
  input  clk,
  input  rst,
  output [3:0] out_1s,
  output [3:0] out_10s,
  output [3:0] out_100s,
  output is_negative
);

  wire [8:0] register_1_q;

  Register #(.width(9)) register_1 (.D({display_2s_comp, data_in}), .en(WE), .clk(clk), .Q(register_1_q), .clr(rst));
  ROM #(.addrWidth(9), .dataWidth(13)) rom_1 (.addr(register_1_q), .data({is_negative, out_100s, out_10s, out_1s}));

  // Notes on the sheet:
  //   Data to display
  //   Is data in 2's complement
  //   contents of rom_1 (hex, n*v repeats v):
  //   0 1 2 3 4 5 6 7 8 9 10 11 12 13 14 15 16 17 18 19 20 21 22 23 24 25 26 27 28 29 30 31 32 33 34 35 36
  //   37 38 39 40 41 42 43 44 45 46 47 48 49 50 51 52 53 54 55 56 57 58 59 60 61 62 63 64 65 66 67 68 69
  //   70 71 72 73 74 75 76 77 78 79 80 81 82 83 84 85 86 87 88 89 90 91 92 93 94 95 96 97 98 99 100 101
  //   102 103 104 105 106 107 108 109 110 111 112 113 114 115 116 117 118 119 120 121 122 123 124 125 126
  //   127 128 129 130 131 132 133 134 135 136 137 138 139 140 141 142 143 144 145 146 147 148 149 150 151
  //   152 153 154 155 156 157 158 159 160 161 162 163 164 165 166 167 168 169 170 171 172 173 174 175 176
  //   177 178 179 180 181 182 183 184 185 186 187 188 189 190 191 192 193 194 195 196 197 198 199 200 201
  //   202 203 204 205 206 207 208 209 210 211 212 213 214 215 216 217 218 219 220 221 222 223 224 225 226
  //   227 228 229 230 231 232 233 234 235 236 237 238 239 240 241 242 243 244 245 246 247 248 249 250 251
  //   252 253 254 255 0 1 2 3 4 5 6 7 8 9 10 11 12 13 14 15 16 17 18 19 20 21 22 23 24 25 26 27 28 29 30
  //   31 32 33 34 35 36 37 38 39 40 41 42 43 44 45 46 47 48 49 50 51 52 53 54 55 56 57 58 59 60 61 62 63
  //   64 65 66 67 68 69 70 71 72 73 74 75 76 77 78 79 80 81 82 83 84 85 86 87 88 89 90 91 92 93 94 95 96
  //   97 98 99 100 101 102 103 104 105 106 107 108 109 110 111 112 113 114 115 116 117 118 119 120 121 122
  //   123 124 125 126 127 1128 1127 1126 1125 1124 1123 1122 1121 1120 1119 1118 1117 1116 1115 1114 1113
  //   1112 1111 1110 1109 1108 1107 1106 1105 1104 1103 1102 1101 1100 1099 1098 1097 1096 1095 1094 1093
  //   1092 1091 1090 1089 1088 1087 1086 1085 1084 1083 1082 1081 1080 1079 1078 1077 1076 1075 1074 1073
  //   1072 1071 1070 1069 1068 1067 1066 1065 1064 1063 1062 1061 1060 1059 1058 1057 1056 1055 1054 1053
  //   1052 1051 1050 1049 1048 1047 1046 1045 1044 1043 1042 1041 1040 1039 1038 1037 1036 1035 1034 1033
  //   1032 1031 1030 1029 1028 1027 1026 1025 1024 1023 1022 1021 1020 1019 1018 1017 1016 1015 1014 1013
  //   1012 1011 1010 1009 1008 1007 1006 1005 1004 1003 1002 1001
endmodule

module Control_Unit (
  input  rst,
  input  clk,
  input  [3:0] instruction,
  input  CF,
  input  ZF,
  output A_out,
  output B_out,
  output hlt,
  output A_in,
  output B_in,
  output A_clr,
  output B_clr,
  output IR_out,
  output MAR_out,
  output IR_in,
  output MAR_in,
  output FLAG_in,
  output IR_clr,
  output MAR_clr,
  output FLAG_clr,
  output EO,
  output PC_en,
  output SU,
  output PC_out,
  output PC_in,
  output PC_clr,
  output OCU_2s,
  output RAM_in,
  output OCU_in,
  output RAM_out,
  output OCU_clr
);

  wire and_1_out, and_2_out, and_3_out, and_4_out, and_5_out, and_6_out, controlled_buffer_2_out,
       controlled_buffer_3_out, d_ff_1_q, decoder_1_out0, decoder_1_out1, JMP_c, JMP_z, nand_1_out,
       nand_2_out, nor_1_out, not_1_out, not_2_out, not_3_out, NXT, or_1_out;
  wire [2:0] counter_1_q;
  wire [18:0] controlled_buffer_1_out;
  wire [23:0] rom_1_data;

  not not_1 (not_1_out, clk);
  Pull_Resistor pull_resistor_1 (.node(A_clr));
  Counter #(.max('h7), .width(3)) counter_1 (
    .Q(counter_1_q), .up(1'b1), .clk(not_1_out), .clr(NXT));  // open: load, D, count, carry
  Pull_Resistor pull_resistor_2 (.node(B_clr));
  Pull_Resistor pull_resistor_3 (.node(IR_clr));
  nor nor_1 (nor_1_out, counter_1_q[2], counter_1_q[1]);
  Pull_Resistor pull_resistor_4 (.node(MAR_out));
  // LedBar #(.inputtype("row"), .matrixcols(3)) ledbar_1: pin names not known; wires that end beside it: counter_1_q
  and and_1 (and_1_out, nor_1_out, counter_1_q[0]);
  Decoder #(.enable("false")) decoder_1 (.out0(decoder_1_out0), .out1(decoder_1_out1), .sel(and_1_out));
  or or_1 (or_1_out, counter_1_q[1], counter_1_q[2]);
  Pull_Resistor pull_resistor_5 (.node(MAR_clr));
  buf buffer_1 (PC_out, and_2_out);
  and and_2 (and_2_out, nor_1_out, decoder_1_out0);
  buf buffer_2 (MAR_in, and_2_out);
  Pull_Resistor pull_resistor_6 (.node(PC_clr));
  ROM #(.addrWidth(7), .dataWidth(24)) rom_1 (.addr({instruction, counter_1_q}), .data(rom_1_data));
  Pull_Resistor pull_resistor_7 (.node(hlt));
  Pull_Resistor pull_resistor_8 (.node(CF));
  Pull_Resistor pull_resistor_9 (.node(ZF));
  buf buffer_3 (RAM_out, decoder_1_out1);
  buf buffer_4 (IR_in, decoder_1_out1);
  buf buffer_5 (PC_en, decoder_1_out1);
  Pull_Resistor pull_resistor_10 (.node(FLAG_clr));
  assign {hlt, MAR_in, RAM_in, RAM_out, IR_in, controlled_buffer_1_out[18], A_in, A_out, B_in, B_out, EO, SU, FLAG_in, OCU_in, OCU_clr, OCU_2s, PC_en, controlled_buffer_1_out[6], PC_out, JMP_c, JMP_z, controlled_buffer_1_out[2:0]} = or_1_out ? rom_1_data : 24'bz;  // Controlled_Buffer controlled_buffer_1
  Pull_Resistor pull_resistor_11 (.node(controlled_buffer_1_out[0]));
  Pull_Resistor pull_resistor_12 (.node(NXT));
  buf buffer_6 (NXT, controlled_buffer_1_out[0]);
  Pull_Resistor pull_resistor_13 (.node(controlled_buffer_1_out[1]));
  Pull_Resistor pull_resistor_14 (.node(controlled_buffer_1_out[2]));
  Pull_Resistor pull_resistor_15 (.node(JMP_z));
  Pull_Resistor pull_resistor_16 (.node(JMP_c));
  Pull_Resistor pull_resistor_17 (.node(PC_out));
  Pull_Resistor pull_resistor_18 (.node(controlled_buffer_1_out[6]));
  Pull_Resistor pull_resistor_19 (.node(PC_in));
  buf buffer_7 (PC_in, controlled_buffer_1_out[6]);
  Pull_Resistor pull_resistor_20 (.node(PC_en));
  Pull_Resistor pull_resistor_21 (.node(OCU_2s));
  Pull_Resistor pull_resistor_22 (.node(OCU_clr));
  Pull_Resistor pull_resistor_23 (.node(OCU_in));
  Pull_Resistor pull_resistor_24 (.node(FLAG_in));
  Pull_Resistor pull_resistor_25 (.node(SU));
  Pull_Resistor pull_resistor_26 (.node(EO));
  Pull_Resistor pull_resistor_27 (.node(B_out));
  Pull_Resistor pull_resistor_28 (.node(B_in));
  Pull_Resistor pull_resistor_29 (.node(A_out));
  Pull_Resistor pull_resistor_30 (.node(A_in));
  Pull_Resistor pull_resistor_31 (.node(controlled_buffer_1_out[18]));
  Pull_Resistor pull_resistor_32 (.node(IR_out));
  buf buffer_8 (IR_out, controlled_buffer_1_out[18]);
  Pull_Resistor pull_resistor_33 (.node(IR_in));
  Pull_Resistor pull_resistor_34 (.node(RAM_out));
  Pull_Resistor pull_resistor_35 (.node(RAM_in));
  Pull_Resistor pull_resistor_36 (.node(MAR_in));
  Pull_Resistor pull_resistor_37 (.node(hlt));
  D_Flip_Flop d_ff_1 (.D(rst), .clk(rst), .Q(d_ff_1_q), .reset(clk));  // open: Qn, preset
  not not_2 (not_2_out, clk);
  not not_3 (not_3_out, clk);
  buf buffer_9 (NXT, d_ff_1_q);
  buf buffer_10 (A_clr, d_ff_1_q);
  buf buffer_11 (B_clr, d_ff_1_q);
  buf buffer_12 (PC_clr, d_ff_1_q);
  buf buffer_13 (IR_clr, d_ff_1_q);
  buf buffer_14 (MAR_clr, d_ff_1_q);
  buf buffer_15 (OCU_clr, d_ff_1_q);
  buf buffer_16 (FLAG_clr, d_ff_1_q);
  and and_3 (and_3_out, ZF, JMP_z);
  buf buffer_17 (IR_out, and_3_out);
  buf buffer_18 (PC_in, and_3_out);
  nand nand_1 (nand_1_out, ZF, JMP_z);
  assign controlled_buffer_2_out = and_4_out ? nand_1_out : 1'bz;  // Controlled_Buffer controlled_buffer_2
  and and_4 (and_4_out, JMP_z, not_2_out);
  and and_5 (and_5_out, CF, JMP_c);
  buf buffer_19 (IR_out, and_5_out);
  buf buffer_20 (PC_in, and_5_out);
  nand nand_2 (nand_2_out, CF, JMP_c);
  assign controlled_buffer_3_out = and_6_out ? nand_2_out : 1'bz;  // Controlled_Buffer controlled_buffer_3
  and and_6 (and_6_out, JMP_c, not_3_out);
  buf buffer_21 (NXT, controlled_buffer_2_out);
  buf buffer_22 (NXT, controlled_buffer_3_out);

  // Notes on the sheet:
  //   Using inverted clock allows CU to perform
  //   logic before the rest of the cpu updates
  //   NXT Control Bit is responsible for ending the current
  //   of the next instruction. Thus, saving CPU cycles
  //   instructions microcode execution and starting the fetch cycle
  //   Control Signal Mapping
  //   Pull down rest of control lines
  //   Enable Microcode Execution
  //   buffer_1 drives only 1 and floats otherwise
  //   buffer_2 drives only 1 and floats otherwise
  //   Perform Instruction Fetch
  //   T1
  //   T0
  //   as the fetch cycle is happening.
  //   contents of rom_1 (hex, n*v repeats v):
  //   400020 180080 6*1 400020 180080 440000 120000 4*1 400020 180080 440000 108000 22800 1 1 1 400020
  //   180080 440000 108000 23800 1 1 1 400020 180080 440000 210000 4*1 400020 180080 60000 5*1 400020
  //   180080 40040 5*1 400020 180080 10 5*1 400020 180080 8 5*1 400020 180080 6*1 400020 180080 6*1 400020
  //   180080 6*1 400020 180080 6*1 400020 180080 200 5*1 400020 180080 10400 5*1 400020 180080 800000 5*1
  //   buffer_3 drives only 1 and floats otherwise
  //   buffer_4 drives only 1 and floats otherwise
  //   buffer_5 drives only 1 and floats otherwise
  //   As far as microcode rom is aware the fetch timing is never seen
  //   Thus, t_x when 000000 is decoded nothing will happen
  //   Microcode Address:
  //   i i i i t t t
  //   i i i i -> Instruction
  //   t t t -> Encoded current micro-code step
  //   buffer_6 drives only 1 and floats otherwise
  //   buffer_7 drives only 1 and floats otherwise
  //   buffer_8 drives only 1 and floats otherwise
  //   Reset Circuit
  //   Note: only reason this works is because program execution starts at address 0x0
  //   If this were not the case, the cpu would fail to load the first instruction
  //   Why choose to use a latch then??? It's an easy solution to clearing the OCU as it needs
  //   a clock pulse to reset. Alternateively you could or the rst signal with the OCU_clr signal.
  //   buffer_9 drives only 1 and floats otherwise
  //   buffer_10 drives only 1 and floats otherwise
  //   buffer_11 drives only 1 and floats otherwise
  //   buffer_12 drives only 1 and floats otherwise
  //   buffer_13 drives only 1 and floats otherwise
  //   buffer_14 drives only 1 and floats otherwise
  //   buffer_15 drives only 1 and floats otherwise
  //   buffer_16 drives only 1 and floats otherwise
  //   It only works now as the MAR is set to 0 during reset thus completeing fetch t0
  //   Conditional Branching Logic
  //   buffer_17 drives only 1 and floats otherwise
  //   buffer_18 drives only 1 and floats otherwise
  //   buffer_19 drives only 1 and floats otherwise
  //   buffer_20 drives only 1 and floats otherwise
  //   buffer_21 drives only 1 and floats otherwise
  //   buffer_22 drives only 1 and floats otherwise
endmodule
